// Logisim project CRC.circ as structural Verilog: 2 circuits, main circuit CRC
module CRC (
  input  [7:0] A,
  input  [3:0] B,
  output [10:0] C
);

  wire [2:0] n4bit_mod2_div_1_c, n4bit_mod2_div_2_c, n4bit_mod2_div_3_c, n4bit_mod2_div_4_c,
       n4bit_mod2_div_5_c, n4bit_mod2_div_6_c, n4bit_mod2_div_7_c;

  _4bit_mod2_div u_4bit_mod2_div_1 (.A(A[7:4]), .B(B), .C(n4bit_mod2_div_1_c));
  _4bit_mod2_div u_4bit_mod2_div_2 (.A({n4bit_mod2_div_1_c, A[3]}), .B(B), .C(n4bit_mod2_div_2_c));
  _4bit_mod2_div u_4bit_mod2_div_3 (.A({n4bit_mod2_div_2_c, A[2]}), .B(B), .C(n4bit_mod2_div_3_c));
  _4bit_mod2_div u_4bit_mod2_div_4 (.A({n4bit_mod2_div_3_c, A[1]}), .B(B), .C(n4bit_mod2_div_4_c));
  _4bit_mod2_div u_4bit_mod2_div_5 (.A({n4bit_mod2_div_4_c, A[0]}), .B(B), .C(n4bit_mod2_div_5_c));
  _4bit_mod2_div u_4bit_mod2_div_6 (.A({n4bit_mod2_div_5_c, 1'b0}), .B(B), .C(n4bit_mod2_div_6_c));
  _4bit_mod2_div u_4bit_mod2_div_7 (.A({n4bit_mod2_div_6_c, 1'b0}), .B(B), .C(n4bit_mod2_div_7_c));
  _4bit_mod2_div u_4bit_mod2_div_8 (.A({n4bit_mod2_div_7_c, 1'b0}), .B(B), .C(C[2:0]));

  assign C[10:3] = A;
endmodule

module _4bit_mod2_div (
  input  [3:0] A,
  input  [3:0] B,
  output [2:0] C
);

  wire [2:0] xor_1_out;

  assign xor_1_out = A[2:0] ^ B[2:0];  // XOR_Gate xor_1, 3 bits wide
  Multiplexer #(.width(3)) multiplexer_1 (.in0(A[2:0]), .in1(xor_1_out), .out(C), .sel(A[3]));  // open: en
endmodule
