// Logisim project fsm.circ as structural Verilog: 3 circuits, main circuit fsm
module fsm (
  input  CLR,
  input  [1:0] In,
  output O
);

  wire CLK_out;
  wire [1:0] multiplexer_1_out, nxtst_1_sn, register_1_q;

  Register #(.width(2)) register_1 (.D(multiplexer_1_out), .Q(register_1_q), .clk(CLK_out));  // open: en, clr
  Multiplexer #(.width(2)) multiplexer_1 (
    .in0(nxtst_1_sn), .in1(2'b00), .out(multiplexer_1_out), .sel(CLR));  // open: en
  Clock CLK (.out(CLK_out));
  nxtst nxtst_1 (.S(register_1_q), .In(In), .Sn(nxtst_1_sn));
  \output  output_1 (.S(register_1_q), .In(In), .O(O));
endmodule

module nxtst (
  input  [1:0] S,
  input  [1:0] In,
  output [1:0] Sn
);

  wire and_1_out, and_2_out, and_3_out, and_4_out, not_1_out, not_2_out, not_3_out, not_4_out, not_5_out,
       not_6_out, not_7_out;

  not not_1 (not_1_out, S[1]);
  not not_2 (not_2_out, In[0]);
  not not_3 (not_3_out, S[0]);
  not not_4 (not_4_out, In[0]);
  not not_5 (not_5_out, In[1]);
  not not_6 (not_6_out, S[0]);
  not not_7 (not_7_out, In[0]);
  and and_1 (and_1_out, not_1_out, S[0], not_2_out);
  and and_2 (and_2_out, S[1], not_3_out, not_4_out);
  and and_3 (and_3_out, not_5_out, In[0]);
  and and_4 (and_4_out, S[1], not_6_out, not_7_out);
  or or_1 (Sn[1], and_1_out, and_2_out);
  or or_2 (Sn[0], and_3_out, and_4_out);
endmodule

module \output  (
  input  [1:0] S,
  input  [1:0] In,
  output O
);

  wire not_1_out, not_2_out;

  not not_1 (not_1_out, S[0]);
  not not_2 (not_2_out, In[0]);
  and and_1 (O, S[1], not_1_out, not_2_out);
endmodule
