// Logisim project grf.circ as structural Verilog: 1 circuit, main circuit grf
module grf (
  input  clk,
  input  reset,
  input  WE,
  input  [4:0] A1,
  input  [4:0] A2,
  input  [4:0] A3,
  input  [31:0] WD,
  output [31:0] RD1,
  output [31:0] RD2
);

  wire We1, We2, We3, We4, We5, We6, We7, We8, We9, We10, We11, We12, We13, We14, We15, We16, We17, We18,
       We19, We20, We21, We22, We23, We24, We25, We26, We27, We28, We29, We30, We31;
  wire [31:0] O1, O2, O3, O4, O5, O6, O7, O8, O9, O10, O11, O12, O13, O14, O15, O16, O17, O18, O19, O20, O21,
       O22, O23, O24, O25, O26, O27, O28, O29, O30, O31;

  Register #(.width(32)) register_1 (.D(WD), .en(We8), .Q(O8), .clk(clk), .clr(reset));
  Register #(.width(32)) register_2 (.D(WD), .en(We16), .Q(O16), .clk(clk), .clr(reset));
  Register #(.width(32)) register_3 (.D(WD), .en(We24), .Q(O24), .clk(clk), .clr(reset));
  Register #(.width(32)) register_4 (.D(WD), .en(We1), .Q(O1), .clk(clk), .clr(reset));
  Register #(.width(32)) register_5 (.D(WD), .en(We9), .Q(O9), .clk(clk), .clr(reset));
  Register #(.width(32)) register_6 (.D(WD), .en(We17), .Q(O17), .clk(clk), .clr(reset));
  Register #(.width(32)) register_7 (.D(WD), .en(We25), .Q(O25), .clk(clk), .clr(reset));
  Register #(.width(32)) register_8 (.D(WD), .en(We2), .Q(O2), .clk(clk), .clr(reset));
  Register #(.width(32)) register_9 (.D(WD), .en(We10), .Q(O10), .clk(clk), .clr(reset));
  Register #(.width(32)) register_10 (.D(WD), .en(We18), .Q(O18), .clk(clk), .clr(reset));
  Register #(.width(32)) register_11 (.D(WD), .en(We26), .Q(O26), .clk(clk), .clr(reset));
  Register #(.width(32)) register_12 (.D(WD), .en(We3), .Q(O3), .clk(clk), .clr(reset));
  Register #(.width(32)) register_13 (.D(WD), .en(We11), .Q(O11), .clk(clk), .clr(reset));
  Register #(.width(32)) register_14 (.D(WD), .en(We19), .Q(O19), .clk(clk), .clr(reset));
  Register #(.width(32)) register_15 (.D(WD), .en(We27), .Q(O27), .clk(clk), .clr(reset));
  Register #(.width(32)) register_16 (.D(WD), .en(We4), .Q(O4), .clk(clk), .clr(reset));
  Register #(.width(32)) register_17 (.D(WD), .en(We12), .Q(O12), .clk(clk), .clr(reset));
  Register #(.width(32)) register_18 (.D(WD), .en(We20), .Q(O20), .clk(clk), .clr(reset));
  Register #(.width(32)) register_19 (.D(WD), .en(We28), .Q(O28), .clk(clk), .clr(reset));
  Register #(.width(32)) register_20 (.D(WD), .en(We5), .Q(O5), .clk(clk), .clr(reset));
  Register #(.width(32)) register_21 (.D(WD), .en(We13), .Q(O13), .clk(clk), .clr(reset));
  Register #(.width(32)) register_22 (.D(WD), .en(We21), .Q(O21), .clk(clk), .clr(reset));
  Register #(.width(32)) register_23 (.D(WD), .en(We29), .Q(O29), .clk(clk), .clr(reset));
  Multiplexer #(.select(5), .width(32)) multiplexer_1 (
    .in0({32{1'b0}}), .in1(O1), .in2(O2), .in3(O3), .in4(O4), .in5(O5), .in6(O6), .in7(O7), .in8(O8),
    .in9(O9), .in10(O10), .in11(O11), .in12(O12), .in13(O13), .in14(O14), .in15(O15), .in16(O16), .in17(O17),
    .in18(O18), .in19(O19), .in20(O20), .in21(O21), .in22(O22), .in23(O23), .in24(O24), .in25(O25),
    .in26(O26), .in27(O27), .in28(O28), .in29(O29), .in30(O30), .in31(O31), .out(RD1), .sel(A1));  // open: en
  Register #(.width(32)) register_24 (.D(WD), .en(We6), .Q(O6), .clk(clk), .clr(reset));
  Register #(.width(32)) register_25 (.D(WD), .en(We14), .Q(O14), .clk(clk), .clr(reset));
  Register #(.width(32)) register_26 (.D(WD), .en(We22), .Q(O22), .clk(clk), .clr(reset));
  Register #(.width(32)) register_27 (.D(WD), .en(We30), .Q(O30), .clk(clk), .clr(reset));
  Register #(.width(32)) register_28 (.D(WD), .en(We7), .Q(O7), .clk(clk), .clr(reset));
  Register #(.width(32)) register_29 (.D(WD), .en(We15), .Q(O15), .clk(clk), .clr(reset));
  Register #(.width(32)) register_30 (.D(WD), .en(We23), .Q(O23), .clk(clk), .clr(reset));
  Register #(.width(32)) register_31 (.D(WD), .en(We31), .Q(O31), .clk(clk), .clr(reset));
  Multiplexer #(.select(5), .width(32)) multiplexer_2 (
    .in0({32{1'b0}}), .in1(O1), .in2(O2), .in3(O3), .in4(O4), .in5(O5), .in6(O6), .in7(O7), .in8(O8),
    .in9(O9), .in10(O10), .in11(O11), .in12(O12), .in13(O13), .in14(O14), .in15(O15), .in16(O16), .in17(O17),
    .in18(O18), .in19(O19), .in20(O20), .in21(O21), .in22(O22), .in23(O23), .in24(O24), .in25(O25),
    .in26(O26), .in27(O27), .in28(O28), .in29(O29), .in30(O30), .in31(O31), .out(RD2), .sel(A2));  // open: en
  Decoder #(.select(5), .disabled(0)) decoder_1 (
    .out1(We1), .out2(We2), .out3(We3), .out4(We4), .out5(We5), .out6(We6), .out7(We7), .out8(We8),
    .out9(We9), .out10(We10), .out11(We11), .out12(We12), .out13(We13), .out14(We14), .out15(We15),
    .out16(We16), .out17(We17), .out18(We18), .out19(We19), .out20(We20), .out21(We21), .out22(We22),
    .out23(We23), .out24(We24), .out25(We25), .out26(We26), .out27(We27), .out28(We28), .out29(We29),
    .out30(We30), .out31(We31), .sel(A3), .en(WE));  // open: out0

  // Other names for the same wires on the sheet: I[31:0] = WD
endmodule
