// Logisim project CPU_P3.circ as structural Verilog: 8 circuits, main circuit main
module main (
  input  reset,
  output [31:0] Instr,
  output RegWrite,
  output [4:0] RegAddr,
  output [31:0] RegData,
  output MemWrite,
  output [4:0] MemAddr,
  output [31:0] MemData
);

  wire ALUSrc, clock_1_out, controller_1_beq, controller_1_bgez, controller_1_bgtz, controller_1_blez,
       controller_1_bltz, controller_1_bne, controller_1_j, controller_1_jr, Equal, EQZ, LTZ, RegDst, SignExt;
  wire [1:0] RegSrc;
  wire [3:0] controller_1_aluop;
  wire [31:0] DMRD, ext_1_imm32, grf_1_rd1, multiplexer_3_out, Result;

  IFU ifu_1 (
    .Equal(Equal), .LTZ(LTZ), .EQZ(EQZ), .Imm32(ext_1_imm32), .Instr(Instr), .Beq(controller_1_beq),
    .Bne(controller_1_bne), .Blez(controller_1_blez), .Bgtz(controller_1_bgtz), .Bltz(controller_1_bltz),
    .Bgez(controller_1_bgez), .J(controller_1_j), .Jr(controller_1_jr), .Clk(clock_1_out), .Reset(reset));  // open: Rs, PC4
  Controller controller_1 (
    .Funct(Instr[5:0]), .Op(Instr[31:26]), .Beq(controller_1_beq), .Bne(controller_1_bne),
    .Blez(controller_1_blez), .Bgtz(controller_1_bgtz), .Bltz(controller_1_bltz), .Bgez(controller_1_bgez),
    .J(controller_1_j), .Jr(controller_1_jr), .RegWrite(RegWrite), .ALUOp(controller_1_aluop),
    .MemWrite(MemWrite), .SignExt(SignExt), .RegDst(RegDst), .RegSrc(RegSrc), .ALUSrc(ALUSrc));
  Multiplexer #(.select(2), .width(32), .enable("false")) multiplexer_1 (
    .in0({Result[31:7], MemAddr, Result[1:0]}), .in1(DMRD), .in2({Instr[15:0], {16{1'b0}}}), .out(RegData),
    .sel(RegSrc));  // open: in3
  Multiplexer #(.width(5), .enable("false")) multiplexer_2 (
    .in0(Instr[20:16]), .in1(Instr[15:11]), .out(RegAddr), .sel(RegDst));
  GRF grf_1 (
    .A1(Instr[25:21]), .A2(Instr[20:16]), .A3(RegAddr), .WD(RegData), .RD1(grf_1_rd1), .RD2(MemData),
    .Clk(clock_1_out), .Reset(reset), .RegWrite(RegWrite));
  EXT ext_1 (.Imm16(Instr[15:0]), .Imm32(ext_1_imm32), .SignExt(SignExt));
  Multiplexer #(.width(32), .enable("false")) multiplexer_3 (
    .in0(MemData), .in1(ext_1_imm32), .out(multiplexer_3_out), .sel(ALUSrc));
  Clock clock_1 (.out(clock_1_out));
  ALU alu_1 (
    .A(grf_1_rd1), .B(multiplexer_3_out), .Result({Result[31:7], MemAddr, Result[1:0]}),
    .ALUOp(controller_1_aluop), .Equal(Equal), .LTZ(LTZ), .EQZ(EQZ));
  DM dm_1 (
    .Addr({Result[31:7], MemAddr, Result[1:0]}), .WD(MemData), .RD(DMRD), .MemWrite(MemWrite),
    .Clk(clock_1_out), .Reset(reset));

  // Other names for the same wires on the sheet: Result[6:2] = MemAddr
endmodule

module BranchCond (
  input  Beq,
  input  Bne,
  input  Blez,
  input  Bgtz,
  input  Bltz,
  input  Bgez,
  input  Equal,
  input  LTZ,
  input  EQZ,
  output Branch
);

  wire and_1_out, and_2_out, and_3_out, and_4_out, and_5_out, and_6_out, not_1_out, not_2_out, not_3_out,
       not_4_out, or_1_out;

  not not_1 (not_1_out, Equal);
  or or_1 (or_1_out, LTZ, EQZ);
  not not_2 (not_2_out, LTZ);
  not not_3 (not_3_out, EQZ);
  not not_4 (not_4_out, LTZ);
  and and_1 (and_1_out, Beq, Equal);
  and and_2 (and_2_out, Bne, not_1_out);
  and and_3 (and_3_out, Blez, or_1_out);
  and and_4 (and_4_out, Bgtz, not_2_out, not_3_out);
  and and_5 (and_5_out, Bltz, LTZ);
  and and_6 (and_6_out, Bgez, not_4_out);
  or or_2 (Branch, and_1_out, and_2_out, and_3_out, and_4_out, and_5_out, and_6_out);
endmodule

module IFU (
  input  Beq,
  input  J,
  input  Jr,
  input  Bne,
  input  Blez,
  input  Bgtz,
  input  Bltz,
  input  Bgez,
  input  Equal,
  input  LTZ,
  input  EQZ,
  input  [31:0] Imm32,
  input  [31:0] Rs,
  input  Clk,
  input  Reset,
  output [31:0] Instr,
  output [31:0] PC4
);

  wire Branch;
  wire [31:0] adder_1_out, multiplexer_1_out, multiplexer_2_out, multiplexer_3_out, PC_q;

  Adder #(.width(32)) adder_1 (.a(PC4), .b({Imm32[29:0], 2'b00}), .out(adder_1_out));  // open: cin, cout
  BranchCond branchcond_1 (
    .Beq(Beq), .Bne(Bne), .Blez(Blez), .Bgtz(Bgtz), .Bltz(Bltz), .Bgez(Bgez), .Equal(Equal), .LTZ(LTZ),
    .EQZ(EQZ), .Branch(Branch));
  Multiplexer #(.width(32), .enable("false")) multiplexer_1 (
    .in0(PC4), .in1(adder_1_out), .out(multiplexer_1_out), .sel(Branch));
  Multiplexer #(.width(32), .enable("false")) multiplexer_2 (
    .in0(multiplexer_1_out), .in1({PC4[31:28], Imm32[25:0], 2'b00}), .out(multiplexer_2_out), .sel(J));
  Multiplexer #(.width(32), .enable("false")) multiplexer_3 (
    .in0(multiplexer_2_out), .in1(Rs), .out(multiplexer_3_out), .sel(Jr));
  Register #(.width(32)) PC (.D(multiplexer_3_out), .Q(PC_q), .clk(Clk), .clr(Reset));  // open: en
  ROM #(.addrWidth(5), .dataWidth(32)) rom_1 (.addr(PC_q[6:2]), .data(Instr));  // open: sel
  Adder #(.width(32)) adder_2 (.a(PC_q), .b(32'h4), .out(PC4));  // open: cin, cout

  // Notes on the sheet:
  //   contents of rom_1 (hex, n*v repeats v):
  //   3c000001 3c010002 3c020003 3c030004 3c040005 3c050006 3c060007 3c070008 3c080009 3c09000a 3c0a000b
  //   3c0b000c 3c0c000d 3c0d000e 3c0e000f 3c0f0010 3c100011 3c110012 3c120013 3c130014 3c140015 3c150016
  //   3c160017 3c170018 3c180019 3c19001a 3c1a001b 3c1b001c 3c1c001d 3c1d001e 3c1e001f 3c1f0020
endmodule

module GRF (
  input  [4:0] A1,
  input  [4:0] A2,
  input  [4:0] A3,
  input  [31:0] WD,
  input  Clk,
  input  Reset,
  input  RegWrite,
  output [31:0] RD1,
  output [31:0] RD2
);

  wire We1, We2, We3, We4, We5, We6, We7, We8, We9, We10, We11, We12, We13, We14, We15, We16, We17, We18,
       We19, We20, We21, We22, We23, We24, We25, We26, We27, We28, We29, We30, We31;
  wire [31:0] O1, O2, O3, O4, O5, O6, O7, O8, O9, O10, O11, O12, O13, O14, O15, O16, O17, O18, O19, O20, O21,
       O22, O23, O24, O25, O26, O27, O28, O29, O30, O31;

  Register #(.width(32)) register_1 (.D(WD), .en(We8), .Q(O8), .clk(Clk), .clr(Reset));
  Register #(.width(32)) register_2 (.D(WD), .en(We16), .Q(O16), .clk(Clk), .clr(Reset));
  Register #(.width(32)) register_3 (.D(WD), .en(We24), .Q(O24), .clk(Clk), .clr(Reset));
  Register #(.width(32)) register_4 (.D(WD), .en(We1), .Q(O1), .clk(Clk), .clr(Reset));
  Register #(.width(32)) register_5 (.D(WD), .en(We9), .Q(O9), .clk(Clk), .clr(Reset));
  Register #(.width(32)) register_6 (.D(WD), .en(We17), .Q(O17), .clk(Clk), .clr(Reset));
  Register #(.width(32)) register_7 (.D(WD), .en(We25), .Q(O25), .clk(Clk), .clr(Reset));
  Register #(.width(32)) register_8 (.D(WD), .en(We2), .Q(O2), .clk(Clk), .clr(Reset));
  Register #(.width(32)) register_9 (.D(WD), .en(We10), .Q(O10), .clk(Clk), .clr(Reset));
  Register #(.width(32)) register_10 (.D(WD), .en(We18), .Q(O18), .clk(Clk), .clr(Reset));
  Register #(.width(32)) register_11 (.D(WD), .en(We26), .Q(O26), .clk(Clk), .clr(Reset));
  Register #(.width(32)) register_12 (.D(WD), .en(We3), .Q(O3), .clk(Clk), .clr(Reset));
  Register #(.width(32)) register_13 (.D(WD), .en(We11), .Q(O11), .clk(Clk), .clr(Reset));
  Register #(.width(32)) register_14 (.D(WD), .en(We19), .Q(O19), .clk(Clk), .clr(Reset));
  Register #(.width(32)) register_15 (.D(WD), .en(We27), .Q(O27), .clk(Clk), .clr(Reset));
  Register #(.width(32)) register_16 (.D(WD), .en(We4), .Q(O4), .clk(Clk), .clr(Reset));
  Register #(.width(32)) register_17 (.D(WD), .en(We12), .Q(O12), .clk(Clk), .clr(Reset));
  Register #(.width(32)) register_18 (.D(WD), .en(We20), .Q(O20), .clk(Clk), .clr(Reset));
  Register #(.width(32)) register_19 (.D(WD), .en(We28), .Q(O28), .clk(Clk), .clr(Reset));
  Register #(.width(32)) register_20 (.D(WD), .en(We5), .Q(O5), .clk(Clk), .clr(Reset));
  Register #(.width(32)) register_21 (.D(WD), .en(We13), .Q(O13), .clk(Clk), .clr(Reset));
  Register #(.width(32)) register_22 (.D(WD), .en(We21), .Q(O21), .clk(Clk), .clr(Reset));
  Register #(.width(32)) register_23 (.D(WD), .en(We29), .Q(O29), .clk(Clk), .clr(Reset));
  Multiplexer #(.select(5), .width(32)) multiplexer_1 (
    .in0({32{1'b0}}), .in1(O1), .in2(O2), .in3(O3), .in4(O4), .in5(O5), .in6(O6), .in7(O7), .in8(O8),
    .in9(O9), .in10(O10), .in11(O11), .in12(O12), .in13(O13), .in14(O14), .in15(O15), .in16(O16), .in17(O17),
    .in18(O18), .in19(O19), .in20(O20), .in21(O21), .in22(O22), .in23(O23), .in24(O24), .in25(O25),
    .in26(O26), .in27(O27), .in28(O28), .in29(O29), .in30(O30), .in31(O31), .out(RD1), .sel(A1));  // open: en
  Register #(.width(32)) register_24 (.D(WD), .en(We6), .Q(O6), .clk(Clk), .clr(Reset));
  Register #(.width(32)) register_25 (.D(WD), .en(We14), .Q(O14), .clk(Clk), .clr(Reset));
  Register #(.width(32)) register_26 (.D(WD), .en(We22), .Q(O22), .clk(Clk), .clr(Reset));
  Register #(.width(32)) register_27 (.D(WD), .en(We30), .Q(O30), .clk(Clk), .clr(Reset));
  Register #(.width(32)) register_28 (.D(WD), .en(We7), .Q(O7), .clk(Clk), .clr(Reset));
  Register #(.width(32)) register_29 (.D(WD), .en(We15), .Q(O15), .clk(Clk), .clr(Reset));
  Register #(.width(32)) register_30 (.D(WD), .en(We23), .Q(O23), .clk(Clk), .clr(Reset));
  Register #(.width(32)) register_31 (.D(WD), .en(We31), .Q(O31), .clk(Clk), .clr(Reset));
  Multiplexer #(.select(5), .width(32)) multiplexer_2 (
    .in0({32{1'b0}}), .in1(O1), .in2(O2), .in3(O3), .in4(O4), .in5(O5), .in6(O6), .in7(O7), .in8(O8),
    .in9(O9), .in10(O10), .in11(O11), .in12(O12), .in13(O13), .in14(O14), .in15(O15), .in16(O16), .in17(O17),
    .in18(O18), .in19(O19), .in20(O20), .in21(O21), .in22(O22), .in23(O23), .in24(O24), .in25(O25),
    .in26(O26), .in27(O27), .in28(O28), .in29(O29), .in30(O30), .in31(O31), .out(RD2), .sel(A2));  // open: en
  Decoder #(.select(5), .disabled(0)) decoder_1 (
    .out1(We1), .out2(We2), .out3(We3), .out4(We4), .out5(We5), .out6(We6), .out7(We7), .out8(We8),
    .out9(We9), .out10(We10), .out11(We11), .out12(We12), .out13(We13), .out14(We14), .out15(We15),
    .out16(We16), .out17(We17), .out18(We18), .out19(We19), .out20(We20), .out21(We21), .out22(We22),
    .out23(We23), .out24(We24), .out25(We25), .out26(We26), .out27(We27), .out28(We28), .out29(We29),
    .out30(We30), .out31(We31), .sel(A3), .en(RegWrite));  // open: out0

  // Other names for the same wires on the sheet: I[31:0] = WD
endmodule

module ALU (
  input  [3:0] ALUOp,
  input  [31:0] A,
  input  [31:0] B,
  output [31:0] Result,
  output Equal,
  output LTZ,
  output EQZ
);

  wire bitselector_1_out;
  wire [31:0] adder_1_out, and_1_out, bit_extender_1_out, multiplexer_1_out, nor_1_out, not_1_out, not_2_out,
       shifter_1_out, shifter_2_out, shifter_3_out, xor_1_out;

  assign not_1_out = ~B;  // NOT_Gate not_1, 32 bits wide
  Adder #(.width(32)) adder_1 (.a(A), .b(multiplexer_1_out), .out(adder_1_out), .cin(ALUOp[0]));  // open: cout
  Multiplexer #(.width(32), .enable("false")) multiplexer_1 (
    .in0(B), .in1(not_1_out), .out(multiplexer_1_out), .sel(ALUOp[0]));
  assign and_1_out = A & B;  // AND_Gate and_1, 32 bits wide
  assign nor_1_out = ~(A | B);  // NOR_Gate nor_1, 32 bits wide
  assign xor_1_out = A ^ B;  // XOR_Gate xor_1, 32 bits wide
  Shifter #(.width(32)) shifter_1 (.in(A), .\dist (B[4:0]), .out(shifter_1_out));
  Shifter #(.width(32), .shift("lr")) shifter_2 (.in(A), .\dist (B[4:0]), .out(shifter_2_out));
  Shifter #(.width(32), .shift("ar")) shifter_3 (.in(A), .\dist (B[4:0]), .out(shifter_3_out));
  assign not_2_out = ~nor_1_out;  // NOT_Gate not_2, 32 bits wide
  Comparator #(.width(32)) comparator_1 (.a(A), .b(B), .eq(Equal));  // open: gt, lt
  BitSelector #(.width(32)) bitselector_1 (.in(adder_1_out), .out(bitselector_1_out), .sel({5{1'b1}}));
  assign bit_extender_1_out = {{31{1'b0}}, bitselector_1_out};  // Bit_Extender bit_extender_1
  Comparator #(.width(32)) comparator_2 (.a(A), .b({32{1'b0}}), .eq(EQZ));  // open: gt, lt
  BitSelector #(.width(32)) bitselector_2 (.in(A), .out(LTZ), .sel({5{1'b1}}));
  Multiplexer #(.select(4), .width(32), .enable("false")) multiplexer_2 (
    .in0(adder_1_out), .in1(adder_1_out), .in2(not_2_out), .in3(and_1_out), .in4(nor_1_out), .in5(xor_1_out),
    .in6(shifter_1_out), .in7(shifter_2_out), .in8(shifter_3_out), .in9(bit_extender_1_out), .out(Result),
    .sel(ALUOp));  // open: in10, in11, in12, in13, in14, in15

  // Other names for the same wires on the sheet: Ctr = ALUOp[0]; BS[4:0] = B[4:0]
endmodule

module DM (
  input  MemWrite,
  input  [31:0] Addr,
  input  Clk,
  input  Reset,
  input  [31:0] WD,
  output [31:0] RD
);

  RAM #(.addrWidth(5), .dataWidth(32), .bus("separate")) ram_1 (
    .addr(Addr[6:2]), .din(WD), .data(RD), .str(MemWrite), .clk(Clk), .clr(Reset));  // open: sel, ld
endmodule

module EXT (
  input  SignExt,
  input  [15:0] Imm16,
  output [31:0] Imm32
);

  wire [31:0] bit_extender_1_out, bit_extender_2_out;

  assign bit_extender_1_out = {{16{1'b0}}, Imm16};  // Bit_Extender bit_extender_1
  assign bit_extender_2_out = {{16{Imm16[15]}}, Imm16};  // Bit_Extender bit_extender_2
  Multiplexer #(.width(32), .enable("false")) multiplexer_1 (
    .in0(bit_extender_1_out), .in1(bit_extender_2_out), .out(Imm32), .sel(SignExt));
endmodule

module Controller (
  input  [5:0] Funct,
  input  [5:0] Op,
  output Beq,
  output Bne,
  output Blez,
  output Bgtz,
  output Bltz,
  output Bgez,
  output J,
  output Jr,
  output RegWrite,
  output [3:0] ALUOp,
  output MemWrite,
  output SignExt,
  output RegDst,
  output [1:0] RegSrc,
  output ALUSrc
);

  wire addu_out, faddu_out, fsubu_out, not_1_out, not_2_out, not_3_out, not_4_out, not_5_out, not_6_out,
       not_7_out, not_9_out, not_10_out, not_11_out, R_out, subu_out;

  not not_1 (not_1_out, Op[5]);
  not not_2 (not_2_out, Op[4]);
  not not_3 (not_3_out, Op[3]);
  not not_4 (not_4_out, Op[2]);
  not not_5 (not_5_out, Op[1]);
  not not_6 (not_6_out, Op[0]);
  and R (R_out, not_1_out, not_2_out, not_3_out, not_4_out, not_5_out, not_6_out);
  and ori (ALUOp[1], not_1_out, not_2_out, Op[3], Op[2], not_5_out, Op[0]);
  and lw (RegSrc[0], Op[5], not_2_out, not_3_out, not_4_out, Op[1], Op[0]);
  and sw (MemWrite, Op[5], not_2_out, Op[3], not_4_out, Op[1], Op[0]);
  and u_beq (Beq, not_1_out, not_2_out, not_3_out, Op[2], not_5_out, not_6_out);
  and lui (RegSrc[1], not_1_out, not_2_out, Op[3], Op[2], Op[1], Op[0]);
  and addu (addu_out, faddu_out, R_out);
  and subu (subu_out, R_out, fsubu_out);
  or u_RegWrite (RegWrite, addu_out, subu_out, ALUOp[1], RegSrc[0], RegSrc[1]);
  and faddu (faddu_out, Funct[5], not_7_out, not_9_out, not_10_out, not_11_out, Funct[0]);
  and fsubu (fsubu_out, Funct[5], not_7_out, not_9_out, not_10_out, Funct[1], Funct[0]);
  not not_7 (not_7_out, Funct[4]);
  // NOT_Gate not_8 has open pins: in=Funct[5], out=open
  or ALUOp0 (ALUOp[0], subu_out, Beq);
  not not_9 (not_9_out, Funct[3]);
  not not_10 (not_10_out, Funct[2]);
  not not_11 (not_11_out, Funct[1]);
  or u_SignExt (SignExt, RegSrc[0], MemWrite, Beq);
  // NOT_Gate not_12 has open pins: in=Funct[0], out=open
  or u_RegDst (RegDst, addu_out, subu_out);
  or u_ALUSrc (ALUSrc, ALUOp[1], RegSrc[0], MemWrite);

  assign ALUOp[3:2] = 2'b00;
  assign Bgez = 1'b0;
  assign Bgtz = 1'b0;
  assign Blez = 1'b0;
  assign Bltz = 1'b0;
  assign Bne = 1'b0;
  assign J = 1'b0;
  assign Jr = 1'b0;
endmodule
