// Logisim project fib32.circ as structural Verilog: 5 circuits, main circuit main
module main (
  input  [31:0] N,
  output [31:0] Nth
);

  wire and_1_out, bitselector_1_out, clock_1_out, comparator_1_eq, comparator_2_gt, or_1_out,
       subtractor_1_bout;
  wire [4:0] bit_extender_1_out;
  wire [5:0] counter_1_q, subtractor_1_out;
  wire [31:0] base_1_o00, base_1_o01, base_1_o10, base_1_o11, matmul_1_o00, matmul_1_o01, matmul_1_o10,
       matmul_1_o11, matrix_1_o00, matrix_1_o01, matrix_1_o10, matrix_1_o11, multiplexer_1_out,
       multiplexer_2_out, multiplexer_3_out, multiplexer_4_out;

  Comparator #(.width(6), .mode("unsigned")) comparator_1 (
    .a({6{1'b0}}), .b(counter_1_q), .eq(comparator_1_eq));  // open: gt, lt
  Multiplexer #(.width(32)) multiplexer_1 (
    .in0(matmul_1_o00), .in1(32'h1), .out(multiplexer_1_out), .sel(comparator_1_eq));  // open: en
  Multiplexer #(.width(32)) multiplexer_2 (
    .in0(matmul_1_o01), .in1({32{1'b0}}), .out(multiplexer_2_out), .sel(comparator_1_eq));  // open: en
  Multiplexer #(.width(32)) multiplexer_3 (
    .in0(matmul_1_o10), .in1({32{1'b0}}), .out(multiplexer_3_out), .sel(comparator_1_eq));  // open: en
  Multiplexer #(.width(32)) multiplexer_4 (
    .in0(matmul_1_o11), .in1(32'h1), .out(multiplexer_4_out), .sel(comparator_1_eq));  // open: en
  Counter #(.width(6), .max('h3f), .ongoal("stay")) counter_1 (
    .Q(counter_1_q), .clk(clock_1_out));  // open: load, D, count, carry, clr
  Clock clock_1 (.out(clock_1_out));
  matrix matrix_1 (
    .I00(multiplexer_1_out), .I01(multiplexer_2_out), .I10(multiplexer_3_out), .I11(multiplexer_4_out),
    .S(or_1_out), .O00(matrix_1_o00), .O01(matrix_1_o01), .O10(matrix_1_o10), .O11(matrix_1_o11));
  base base_1 (.CNT(counter_1_q), .O00(base_1_o00), .O01(base_1_o01), .O10(base_1_o10), .O11(base_1_o11));
  Bit_Extender #(.in_width(6), .out_width(5)) bit_extender_1 (.in(subtractor_1_out), .out(bit_extender_1_out));
  Subtractor #(.width(6)) subtractor_1 (
    .a(counter_1_q), .b(6'b000001), .out(subtractor_1_out), .bout(subtractor_1_bout));  // open: bin
  matmul matmul_1 (
    .I100(matrix_1_o00), .I101(matrix_1_o01), .I110(matrix_1_o10), .I111(matrix_1_o11), .I200(base_1_o00),
    .I201(base_1_o01), .I210(base_1_o10), .I211(base_1_o11), .O00(matmul_1_o00), .O01(matmul_1_o01),
    .O10(matmul_1_o10), .O11(matmul_1_o11));
  BitSelector #(.width(32)) bitselector_1 (.in(N), .out(bitselector_1_out), .sel(bit_extender_1_out));
  and and_1 (and_1_out, bitselector_1_out, ~comparator_2_gt, ~subtractor_1_bout);  // AND_Gate
  Comparator #(.width(6), .mode("unsigned")) comparator_2 (
    .a(counter_1_q), .b(6'b100000), .gt(comparator_2_gt));  // open: eq, lt
  or or_1 (or_1_out, and_1_out, subtractor_1_bout);
  \output  output_1 (.In(matrix_1_o01), .OK(comparator_2_gt), .Nth(Nth));
endmodule

module matrix (
  input  [31:0] I00,
  input  [31:0] I01,
  input  [31:0] I10,
  input  [31:0] I11,
  input  S,
  output [31:0] O00,
  output [31:0] O01,
  output [31:0] O10,
  output [31:0] O11
);

  wire clock_1_out;

  Register #(.width(32)) register_1 (.D(I00), .en(S), .Q(O00), .clk(clock_1_out));  // open: clr
  Register #(.width(32)) register_2 (.D(I01), .en(S), .Q(O01), .clk(clock_1_out));  // open: clr
  Register #(.width(32)) register_3 (.D(I10), .en(S), .Q(O10), .clk(clock_1_out));  // open: clr
  Register #(.width(32)) register_4 (.D(I11), .en(S), .Q(O11), .clk(clock_1_out));  // open: clr
  Clock clock_1 (.out(clock_1_out));
endmodule

module \output  (
  input  [31:0] In,
  input  OK,
  output [31:0] Nth
);

  Multiplexer #(.width(32)) multiplexer_1 (.in0({32{1'b0}}), .in1(In), .out(Nth), .sel(OK));  // open: en
endmodule

module matmul (
  input  [31:0] I100,
  input  [31:0] I101,
  input  [31:0] I110,
  input  [31:0] I111,
  input  [31:0] I200,
  input  [31:0] I201,
  input  [31:0] I210,
  input  [31:0] I211,
  output [31:0] O00,
  output [31:0] O01,
  output [31:0] O10,
  output [31:0] O11
);

  wire [31:0] multiplier_1_out, multiplier_2_out, multiplier_3_out, multiplier_4_out, multiplier_5_out,
       multiplier_6_out, multiplier_7_out, multiplier_8_out;

  Multiplier #(.width(32)) multiplier_1 (.a(I100), .b(I200), .out(multiplier_1_out));  // open: cin, cout
  Multiplier #(.width(32)) multiplier_2 (.a(I101), .b(I210), .out(multiplier_2_out));  // open: cin, cout
  Multiplier #(.width(32)) multiplier_3 (.a(I100), .b(I201), .out(multiplier_3_out));  // open: cin, cout
  Multiplier #(.width(32)) multiplier_4 (.a(I101), .b(I211), .out(multiplier_4_out));  // open: cin, cout
  Multiplier #(.width(32)) multiplier_5 (.a(I110), .b(I200), .out(multiplier_5_out));  // open: cin, cout
  Multiplier #(.width(32)) multiplier_6 (.a(I111), .b(I210), .out(multiplier_6_out));  // open: cin, cout
  Multiplier #(.width(32)) multiplier_7 (.a(I110), .b(I201), .out(multiplier_7_out));  // open: cin, cout
  Multiplier #(.width(32)) multiplier_8 (.a(I111), .b(I211), .out(multiplier_8_out));  // open: cin, cout
  Adder #(.width(32)) adder_1 (.a(multiplier_1_out), .b(multiplier_2_out), .out(O00));  // open: cin, cout
  Adder #(.width(32)) adder_2 (.a(multiplier_3_out), .b(multiplier_4_out), .out(O01));  // open: cin, cout
  Adder #(.width(32)) adder_3 (.a(multiplier_5_out), .b(multiplier_6_out), .out(O10));  // open: cin, cout
  Adder #(.width(32)) adder_4 (.a(multiplier_7_out), .b(multiplier_8_out), .out(O11));  // open: cin, cout
endmodule

module base (
  input  [5:0] CNT,
  output [31:0] O00,
  output [31:0] O01,
  output [31:0] O10,
  output [31:0] O11
);

  wire comparator_1_eq;
  wire [31:0] multiplexer_1_out, multiplexer_2_out, multiplexer_3_out, multiplexer_4_out, O00_t, O01_t,
       O10_t, O11_t;

  Comparator #(.width(6), .mode("unsigned")) comparator_1 (
    .a(CNT), .b({6{1'b0}}), .eq(comparator_1_eq));  // open: gt, lt
  Multiplexer #(.width(32)) multiplexer_1 (
    .in0(O00_t), .in1(32'h1), .out(multiplexer_1_out), .sel(comparator_1_eq));  // open: en
  Multiplexer #(.width(32)) multiplexer_2 (
    .in0(O01_t), .in1(32'h1), .out(multiplexer_2_out), .sel(comparator_1_eq));  // open: en
  Multiplexer #(.width(32)) multiplexer_3 (
    .in0(O10_t), .in1(32'h1), .out(multiplexer_3_out), .sel(comparator_1_eq));  // open: en
  Multiplexer #(.width(32)) multiplexer_4 (
    .in0(O11_t), .in1({32{1'b0}}), .out(multiplexer_4_out), .sel(comparator_1_eq));  // open: en
  matrix matrix_1 (
    .I00(multiplexer_1_out), .I01(multiplexer_2_out), .I10(multiplexer_3_out), .I11(multiplexer_4_out),
    .S(1'b1), .O00(O00), .O01(O01), .O10(O10), .O11(O11));
  matmul matmul_1 (
    .I100(O00), .I101(O01), .I110(O10), .I111(O11), .I200(O00), .I201(O01), .I210(O10), .I211(O11),
    .O00(O00_t), .O01(O01_t), .O10(O10_t), .O11(O11_t));
endmodule
