// Logisim project fib4.circ as structural Verilog: 1 circuit, main circuit main
module main (
  input  [2:0] N,
  output [3:0] Nth
);

  wire bitselector_1_out, bitselector_2_out, clock_1_out, comparator_1_eq, comparator_2_eq, comparator_2_lt,
       en, nor_1_out, or_1_out;
  wire [2:0] cnt;
  wire [3:0] adder_1_out, demultiplexer_1_out0, demultiplexer_1_out1, multiplexer_1_out, register_1_q,
       register_2_q;

  Clock clock_1 (.out(clock_1_out));
  Comparator #(.width(3), .mode("unsigned")) comparator_1 (.a(cnt), .b(3'b000), .eq(comparator_1_eq));  // open: gt, lt
  Adder #(.width(4)) adder_1 (
    .a(register_1_q), .b(register_2_q), .out(adder_1_out), .cin(comparator_1_eq));  // open: cout
  Demultiplexer #(.width(4)) demultiplexer_1 (
    .out0(demultiplexer_1_out0), .out1(demultiplexer_1_out1), .in(adder_1_out), .sel(bitselector_1_out));  // open: en
  BitSelector #(.width(3)) bitselector_1 (.in(cnt), .out(bitselector_1_out), .sel(2'b00));
  Counter #(.width(3), .max('h7), .ongoal("stay")) counter_1 (
    .Q(cnt), .clk(clock_1_out));  // open: load, D, count, carry, clr
  Register #(.width(4)) register_1 (
    .D(demultiplexer_1_out0), .en(nor_1_out), .Q(register_1_q), .clk(clock_1_out));  // open: clr
  Register #(.width(4)) register_2 (
    .D(demultiplexer_1_out1), .en(en), .Q(register_2_q), .clk(clock_1_out));  // open: clr
  BitSelector #(.width(3)) bitselector_2 (.in(N), .out(bitselector_2_out), .sel(2'b00));
  Comparator #(.width(3), .mode("unsigned")) comparator_2 (
    .a(N), .b(cnt), .eq(comparator_2_eq), .lt(comparator_2_lt));  // open: gt
  and and_1 (en, bitselector_1_out, ~or_1_out);  // AND_Gate
  Multiplexer #(.width(4)) multiplexer_1 (
    .in0(register_2_q), .in1(register_1_q), .out(multiplexer_1_out), .sel(bitselector_2_out));  // open: en
  nor nor_1 (nor_1_out, bitselector_1_out, or_1_out);
  or or_1 (or_1_out, comparator_2_eq, comparator_2_lt);
  Multiplexer #(.width(4)) multiplexer_2 (
    .in0(4'b0000), .in1(multiplexer_1_out), .out(Nth), .sel(or_1_out));  // open: en
endmodule
