// Logisim project mod5.circ as structural Verilog: 3 circuits, main circuit mod5
module mod5 (
  input  In,
  output out_2,
  output out_3,
  output out_4,
  output out_5,
  output out_6
);

  wire clock_1_out, d_ff_1_q, nexts_1_sp;

  Clock clock_1 (.out(clock_1_out));
  nextS nexts_1 (.In(In), .S(d_ff_1_q), .Sp(nexts_1_sp));
  D_Flip_Flop d_ff_1 (.clk(clock_1_out), .D(nexts_1_sp), .Q(d_ff_1_q));  // open: Qn, preset, en, reset
  \output  output_1 (.S(d_ff_1_q), .In(In), .S0(out_2), .S1(out_3), .S2(out_4), .S3(out_5), .S4(out_6));
endmodule

module nextS (
  input  In,
  input  S,
  output Sp
);


  assign Sp = In;
endmodule

module \output  (
  input  S,
  input  In,
  output S0,
  output S1,
  output S2,
  output S3,
  output S4
);

  wire not_1_out, not_2_out, not_3_out, not_4_out;

  not not_1 (not_1_out, S);
  not not_2 (not_2_out, In);
  not not_3 (not_3_out, S);
  and and_1 (S3, S, In);
  not not_4 (not_4_out, In);
  and and_2 (S1, not_1_out, not_2_out);
  and and_3 (S2, not_3_out, In);
  and and_4 (S4, S, not_4_out);

  assign S0 = 1'b0;
endmodule
